# Fritzing sketch arduino_nano_connections (saved by Fritzing 0.9.3b)

parts:
  Engine = Basic Servo
  Part1 = Arduino Nano (Rev3.0) (ICSP)
  J1 = Basic Servo

nets:
  N1: Engine.pulse, Part1.D5
  N2: Part1.D6, J1.pulse
  GND: Part1.GND, J1.gnd
  5V: Part1.5V, J1.vcc
